# Fritzing sketch Schaltplan (saved by Fritzing 0.9.3b)
circuit board: 8.46667cm x 5.64444cm
breadboards: 1

parts:
  Bauteil1 = Arduino Nano (Rev3.0)
  S1 = Pushbutton [package="[THT]"]
  S2 = Pushbutton [package="[THT]"]
  S3 = Pushbutton [package="[THT]"]
  R1 = Resistor [tolerance=±5% resistance=10k package=THT]
  R2 = Resistor [tolerance=±5% resistance=10k package=THT]
  R3 = Resistor [tolerance=±5% resistance=10k package=THT]
  ZS-042_RTC1 = ZS-042 RTC Module
  Grove1 = Grove 4 Digit Display
  D1 = LTE-302 [package=lte-302]
  Q1 = Basic FET P-Channel [package="TO220 [THT]"]
  R4 = Resistor [tolerance=±5% resistance=10k package=THT]
  Power_plug1 = Power plug

nets:
  GND: Bauteil1.GND, R1.Pin_0, R3.Pin_0, ZS-042_RTC1.GND, Grove1.GND
  N1: Bauteil1.D4, Grove1.CLK
  N2: Bauteil1.D5, Grove1.DIO
  N3: Bauteil1.D9, R4.Pin_1
  N4: Bauteil1.D10, S1.Pin_1, S1.Pin_2, R3.Pin_1
  N5: Bauteil1.D11/MOSI, S2.Pin_1, S2.Pin_2, R2.Pin_1
  N6: Bauteil1.D12/MISO, S3.Pin_1, S3.Pin_2, R1.Pin_1
  VCC: Bauteil1.5V, S1.Pin_3, S1.Pin_4, S2.Pin_3, S2.Pin_4, S3.Pin_3, S3.Pin_4, ZS-042_RTC1.VCC, Grove1.VCC
  N7: Bauteil1.A5, ZS-042_RTC1.SCL
  N8: Bauteil1.A4, ZS-042_RTC1.SDA
  N9: D1.A, Power_plug1.GND
  N10: D1.C, Q1.source
  N11: Q1.gate, R4.Pin_0
  N12: Q1.drain, Power_plug1.VCC
